# Fritzing sketch schemas (saved by Fritzing 0.9.3b)
breadboards: 1

parts:
  Composant1 = Arduino Nano (Rev3.0) (ICSP)
  SP1 = SPEAKER [package=pcb_mount_speaker]
  Q1 = npn-Powertransistor [package="TO220 [THT]"]
  LED1 = smd LED [color="White (4500K)" package="0805 [SMD]"]
  R2 = Resistor [tolerance=±5% resistance=220 package=THT]
  LED2 = smd LED [color="White (4500K)" package="0805 [SMD]"]
  S1 = Momentary Switch [package=ksa_sealed_tac_switch]
  R3 = Resistor [tolerance=±5% resistance=220 package=THT]
  R4 = Resistor [tolerance=±5% resistance=220 package=THT]
  BAT1 = BC9VPC [package=bc9vpc]
  Composant2 = Arduino Nano (Rev3.0) (ICSP)
  SP2 = SPEAKER [package=pcb_mount_speaker]
  Q2 = npn-Powertransistor [package="TO220 [THT]"]
  R6 = Resistor [tolerance=±5% resistance=220 package=THT]
  S2 = Momentary Switch [package=ksa_sealed_tac_switch]
  R7 = Resistor [tolerance=±5% resistance=220 package=THT]
  BAT2 = BC9VPC [package=bc9vpc]
  LED5 = smd LED [color="Yellow (595nm)" package="0805 [SMD]"]
  LED6 = smd LED [color="Yellow (595nm)" package="0805 [SMD]"]
  R8 = Resistor [tolerance=±5% resistance=220 package="2512 [SMD]"]

nets (from the breadboard view):
  N1: Composant1.GND, Q1.emitter, LED2.cathode, R3.Pin_0, BAT1.V-
  N2: Composant1.D2, S1.2
  N3: Composant1.D7, R2.Pin_0
  N4: Composant1.D11/MOSI, Q1.base
  N5: Composant1.VIN, BAT1.V+
  N6: Composant1.5V, SP1.-, R4.Pin_1
  N7: SP1.+, Q1.collector
  N8: LED1.anode, R2.Pin_1, LED2.anode
  N9: S1.1, R3.Pin_1
  N10: S1.3, R4.Pin_0
  N11: Composant2.GND, Q2.emitter, BAT2.V-, LED5.cathode, LED6.cathode, R8.Pin_0
  N12: Composant2.D2, S2.2, R8.Pin_1
  N13: Composant2.D7, R7.Pin_1
  N14: Composant2.D11/MOSI, Q2.base
  N15: Composant2.VIN, BAT2.V+
  N16: Composant2.5V, SP2.-, R6.Pin_1
  N17: SP2.+, Q2.collector
  N18: R6.Pin_0, S2.3
  N19: R7.Pin_0, LED5.anode, LED6.anode
